// Logisim project AiAlu.circ as structural Verilog
module ArithUnit (
  input  a0,
  input  a1,
  input  a2,
  input  a3,
  input  a4,
  input  a5,
  input  a6,
  input  a7,
  input  b0,
  input  b1,
  input  b2,
  input  b3,
  input  b4,
  input  b5,
  input  b6,
  input  b7,
  input  [1:0] Operation_Select,
  output [7:0] out_18,
  output out_19
);

  wire button_1_out, operation_selector_1_p2, operation_selector_1_p3;
  wire [7:0] cpl2_1_p4;

  Button button_1 (.out(button_1_out));
  // Operation_Selector operation_selector_1: pin names not known; wires that end beside it: out_19, operation_selector_1_p2, operation_selector_1_p3
  // Processor_Enabler processor_enabler_1: pin names not known; wires that end beside it: operation_selector_1_p2
  // Intel_Adder_8_bit intel_adder_8_bit_1: pin names not known; wires that end beside it: button_1_out
  // Processor_Enabler_AUX processor_enabler_aux_1: pin names not known; wires that end beside it: operation_selector_1_p2, out_18
  // Processor_Enabler processor_enabler_2: pin names not known
  // Cpl2 cpl2_1: pin names not known; wires that end beside it: operation_selector_1_p3, button_1_out, operation_selector_1_p3, cpl2_1_p4[0], cpl2_1_p4[1], cpl2_1_p4[2], cpl2_1_p4[3], cpl2_1_p4[4], cpl2_1_p4[5], cpl2_1_p4[6], cpl2_1_p4[7]
  // Processor_Enabler_AUX processor_enabler_aux_2: pin names not known
  // Result_Confirmer result_confirmer_1: pin names not known
endmodule

module Cpl2 (
  input  a0,
  input  a1,
  input  a2,
  input  a3,
  input  a4,
  input  a5,
  input  a6,
  input  a7,
  input  b0,
  input  c,
  input  b1,
  input  b2,
  input  b3,
  input  b4,
  input  b5,
  input  b6,
  input  b7,
  output y0,
  output y1,
  output y2,
  output y3,
  output y4,
  output y5,
  output y6,
  output y7
);

  wire intel_adder_8_bit_1_p1, intel_adder_8_bit_1_p2, intel_adder_8_bit_1_p3, intel_adder_8_bit_1_p4,
       intel_adder_8_bit_1_p6, intel_adder_8_bit_1_p7, intel_adder_8_bit_1_p8, intel_adder_8_bit_1_p9,
       intel_adder_8_bit_1_p10;

  // NOT_Gate not_1 has open pins: in=b0, out=open
  // NOT_Gate not_2 has open pins: in=b1, out=open
  // NOT_Gate not_3 has open pins: in=b2, out=open
  // NOT_Gate not_4 has open pins: in=b3, out=open
  // NOT_Gate not_5 has open pins: in=b4, out=open
  // NOT_Gate not_6 has open pins: in=b5, out=open
  // NOT_Gate not_7 has open pins: in=b6, out=open
  // NOT_Gate not_8 has open pins: in=b7, out=open
  // Intel_Adder_8_bit intel_adder_8_bit_1: pin names not known; wires that end beside it: intel_adder_8_bit_1_p1, intel_adder_8_bit_1_p2, intel_adder_8_bit_1_p3, intel_adder_8_bit_1_p4, 1'b1, intel_adder_8_bit_1_p6, intel_adder_8_bit_1_p7, intel_adder_8_bit_1_p8, intel_adder_8_bit_1_p9, intel_adder_8_bit_1_p10, 1'b0, 1'b0, 1'b0, 1'b0, 1'b0, 1'b0, 1'b0, 1'b0
  // Intel_Adder_8_bit intel_adder_8_bit_2: pin names not known; wires that end beside it: c, a0, intel_adder_8_bit_1_p9, a1, intel_adder_8_bit_1_p8, a2, intel_adder_8_bit_1_p7, a3, intel_adder_8_bit_1_p6, a4, intel_adder_8_bit_1_p4, a5, intel_adder_8_bit_1_p3, a6, intel_adder_8_bit_1_p2, a7, intel_adder_8_bit_1_p1, y0, y1, y2, y3, y4, y5, y6, y7, intel_adder_8_bit_1_p10
endmodule

module and8bit (
  input  [7:0] aand,
  input  [7:0] band,
  output [7:0] yand
);

  assign yand = aand & band;  // AND_Gate and_1, 8 bits wide
endmodule

module or8bit (
  input  [7:0] aor,
  input  [7:0] bor,
  output [7:0] yor
);

  assign yor = aor | bor;  // OR_Gate or_1, 8 bits wide
endmodule

module not8bit (
  input  [7:0] in_1,
  input  [7:0] in_2
);

  // NOT_Gate not_1 is placed but not wired
endmodule
